# Fritzing sketch wemos_wio_plaque_essais (saved by Fritzing 0.9.3b)
stripboards: 1

parts:
  S1 = Pushbutton [package="[THT]"]
  Grove1 = Grove Button  # not connected
  Grove2 = Grove Button  # not connected
  R1 = Resistor [tolerance=±5% resistance=100k package=THT]
  R2 = Resistor [tolerance=±5% resistance=100k package=THT]
  R3 = Resistor [tolerance=±5% resistance=100k package=THT]
  J1 = female pin header, 8 pins [form="♀ (female)"]
  J2 = female pin header, 8 pins [form="♀ (female)"]

nets:
  N1: S1.Pin_1, S1.Pin_2, J2.pin4
  N2: S1.Pin_3, S1.Pin_4, R1.Pin_1, J2.pin2
  N3: R1.Pin_0, R2.Pin_1, J1.pin7
  N4: R2.Pin_0, R3.Pin_1
  N5: R3.Pin_0, J2.pin6

custom parts:
  Grove Button: A button
