# Fritzing sketch wemos_wio_sch (saved by Fritzing 0.9.3b)

parts:
  WeMos_D1_Mini1 = WeMos D1 Mini
  R1 = Resistor [tolerance=±5% resistance=100k package=THT]
  R2 = Resistor [tolerance=±5% resistance=100k package=THT]
  R3 = Resistor [tolerance=±5% resistance=100k package=THT]
  S1 = Pushbutton [package="[THT]"]
  Grove1 = Grove Button
  Grove2 = Grove Button

nets:
  N1: WeMos_D1_Mini1.A0, R1.Pin_0, R2.Pin_1
  N2: WeMos_D1_Mini1.D1, R3.Pin_1, Grove2.SIG
  N3: WeMos_D1_Mini1.D2, Grove2.NC
  N4: WeMos_D1_Mini1.D3, S1.Pin_4
  GND: WeMos_D1_Mini1.G, R2.Pin_0, S1.Pin_1, S1.Pin_2, Grove1.GND, Grove2.GND
  N5: WeMos_D1_Mini1.RX, Grove1.SIG
  N6: WeMos_D1_Mini1.TX, Grove1.NC
  N7: R1.Pin_1, R3.Pin_0

notes:
  Bt fonction

custom parts:
  Grove Button: A button
